// Digital circuit 8bit-ALU.dig as structural Verilog
module _8bit_ALU (
  input  s2,
  input  s3,
  input  A7,
  input  A6,
  input  A5,
  input  A4,
  input  A3,
  input  A2,
  input  A1,
  input  A0,
  input  common_CLK,
  input  B7,
  input  B6,
  input  B5,
  input  B4,
  input  B3,
  input  B2,
  input  B1,
  input  B0,
  input  S0,
  input  S1,
  output [7:0] OUTPUT
);

  wire multiplexer_1_out, multiplexer_2_out, multiplexer_3_out, multiplexer_4_out, multiplexer_5_out,
       multiplexer_6_out, multiplexer_7_out, multiplexer_8_out, multiplexer_10_out, multiplexer_12_out;
  wire [7:0] add_1_s, and_1_out, d_ff_1_q, d_ff_2_q, d_ff_6_q, multiplexer_9_out, multiplexer_11_out,
       multiplexer_13_out, not_1_out, or_1_out, xor_1_out;

  Multiplexer #(.Selector_Bits(2)) multiplexer_1 (
    .sel({S1, S0}), .in_0(1'b0), .in_1(d_ff_6_q[6]), .in_2(multiplexer_1_out), .in_3(d_ff_6_q[6]),
    .out(multiplexer_1_out));
  D_FF d_ff_1 (.D(A7), .C(common_CLK), .Q(d_ff_1_q[7]));  // open: nQ
  D_FF d_ff_2 (.D(B7), .C(common_CLK), .Q(d_ff_2_q[7]));  // open: nQ
  Multiplexer #(.Selector_Bits(2)) multiplexer_2 (
    .sel({S1, S0}), .in_0(d_ff_6_q[7]), .in_1(d_ff_6_q[5]), .in_2(d_ff_6_q[7]), .in_3(d_ff_6_q[5]),
    .out(multiplexer_2_out));
  D_FF d_ff_3 (.D(multiplexer_1_out), .C(common_CLK), .Q(d_ff_6_q[7]));  // open: nQ
  D_FF d_ff_4 (.D(A6), .C(common_CLK), .Q(d_ff_1_q[6]));  // open: nQ
  D_FF d_ff_5 (.D(B6), .C(common_CLK), .Q(d_ff_2_q[6]));  // open: nQ
  D_FF d_ff_6 (.D(multiplexer_2_out), .C(common_CLK), .Q(d_ff_6_q[6]));  // open: nQ
  Multiplexer #(.Selector_Bits(2)) multiplexer_3 (
    .sel({S1, S0}), .in_0(d_ff_6_q[6]), .in_1(d_ff_6_q[4]), .in_2(d_ff_6_q[6]), .in_3(d_ff_6_q[4]),
    .out(multiplexer_3_out));
  D_FF d_ff_7 (.D(A5), .C(common_CLK), .Q(d_ff_1_q[5]));  // open: nQ
  D_FF d_ff_8 (.D(B5), .C(common_CLK), .Q(d_ff_2_q[5]));  // open: nQ
  Multiplexer #(.Selector_Bits(2)) multiplexer_4 (
    .sel({S1, S0}), .in_0(d_ff_6_q[5]), .in_1(d_ff_6_q[3]), .in_2(d_ff_6_q[5]), .in_3(d_ff_6_q[3]),
    .out(multiplexer_4_out));
  D_FF d_ff_9 (.D(multiplexer_3_out), .C(common_CLK), .Q(d_ff_6_q[5]));  // open: nQ
  D_FF d_ff_10 (.D(A4), .C(common_CLK), .Q(d_ff_1_q[4]));  // open: nQ
  D_FF d_ff_11 (.D(B4), .C(common_CLK), .Q(d_ff_2_q[4]));  // open: nQ
  D_FF d_ff_12 (.D(multiplexer_4_out), .C(common_CLK), .Q(d_ff_6_q[4]));  // open: nQ
  Multiplexer #(.Selector_Bits(2)) multiplexer_5 (
    .sel({S1, S0}), .in_0(d_ff_6_q[4]), .in_1(d_ff_6_q[2]), .in_2(d_ff_6_q[4]), .in_3(d_ff_6_q[2]),
    .out(multiplexer_5_out));
  D_FF d_ff_13 (.D(A3), .C(common_CLK), .Q(d_ff_1_q[3]));  // open: nQ
  D_FF d_ff_14 (.D(B3), .C(common_CLK), .Q(d_ff_2_q[3]));  // open: nQ
  Multiplexer #(.Selector_Bits(2)) multiplexer_6 (
    .sel({S1, S0}), .in_0(d_ff_6_q[3]), .in_1(d_ff_6_q[1]), .in_2(d_ff_6_q[3]), .in_3(d_ff_6_q[1]),
    .out(multiplexer_6_out));
  D_FF d_ff_15 (.D(multiplexer_5_out), .C(common_CLK), .Q(d_ff_6_q[3]));  // open: nQ
  D_FF d_ff_16 (.D(A2), .C(common_CLK), .Q(d_ff_1_q[2]));  // open: nQ
  D_FF d_ff_17 (.D(B2), .C(common_CLK), .Q(d_ff_2_q[2]));  // open: nQ
  D_FF d_ff_18 (.D(multiplexer_6_out), .C(common_CLK), .Q(d_ff_6_q[2]));  // open: nQ
  Multiplexer #(.Selector_Bits(2)) multiplexer_7 (
    .sel({S1, S0}), .in_0(d_ff_6_q[2]), .in_1(d_ff_6_q[0]), .in_2(d_ff_6_q[2]), .in_3(d_ff_6_q[0]),
    .out(multiplexer_7_out));
  D_FF d_ff_19 (.D(A1), .C(common_CLK), .Q(d_ff_1_q[1]));  // open: nQ
  D_FF d_ff_20 (.D(B1), .C(common_CLK), .Q(d_ff_2_q[1]));  // open: nQ
  Multiplexer #(.Selector_Bits(2)) multiplexer_8 (
    .sel({S1, S0}), .in_0(d_ff_6_q[1]), .in_1(1'b0), .in_2(d_ff_6_q[1]), .in_3(1'b0), .out(multiplexer_8_out));
  D_FF d_ff_21 (.D(multiplexer_7_out), .C(common_CLK), .Q(d_ff_6_q[1]));  // open: nQ
  D_FF d_ff_22 (.D(A0), .C(common_CLK), .Q(d_ff_1_q[0]));  // open: nQ
  D_FF d_ff_23 (.D(B0), .C(common_CLK), .Q(d_ff_2_q[0]));  // open: nQ
  D_FF d_ff_24 (.D(multiplexer_8_out), .C(common_CLK), .Q(d_ff_6_q[0]));  // open: nQ
  assign and_1_out = d_ff_1_q & d_ff_2_q;  // And and_1, 8 bits wide
  assign or_1_out = d_ff_1_q | d_ff_2_q;  // Or or_1, 8 bits wide
  assign xor_1_out = d_ff_1_q ^ d_ff_2_q;  // XOr xor_1, 8 bits wide
  Multiplexer #(.Bits(8)) multiplexer_9 (.sel(s2), .in_0({8{1'b0}}), .in_1({8{1'b1}}), .out(multiplexer_9_out));
  assign not_1_out = ~d_ff_2_q;  // Not not_1, 8 bits wide
  Multiplexer multiplexer_10 (.sel(s2), .in_0(1'b1), .in_1(1'b0), .out(multiplexer_10_out));
  Multiplexer #(.Selector_Bits(2), .Bits(8)) multiplexer_11 (
    .sel({S1, S0}), .in_0(multiplexer_9_out), .in_1(d_ff_2_q), .in_2(not_1_out), .in_3(not_1_out),
    .out(multiplexer_11_out));
  Multiplexer #(.Selector_Bits(2)) multiplexer_12 (
    .sel({S1, S0}), .in_0(multiplexer_10_out), .in_1(1'b1), .in_2(1'b0), .in_3(1'b1), .out(multiplexer_12_out));
  Multiplexer #(.Selector_Bits(2), .Bits(8)) multiplexer_13 (
    .sel({S1, S0}), .in_0(d_ff_1_q), .in_1(and_1_out), .in_2(or_1_out), .in_3(xor_1_out),
    .out(multiplexer_13_out));
  Add #(.Bits(8)) add_1 (.a(d_ff_1_q), .b(multiplexer_11_out), .c_i(multiplexer_12_out), .s(add_1_s));  // open: c_o
  Multiplexer #(.Selector_Bits(2), .Bits(8)) multiplexer_14 (
    .sel({s3, s2}), .in_0(multiplexer_13_out), .in_1(d_ff_6_q), .in_2(add_1_s), .in_3(add_1_s), .out(OUTPUT));
endmodule
